// Logisim project cu (2).circ as structural Verilog: 1 circuit, main circuit select registro
module select_registro (
  input  in_1,
  input  [31:0] A,
  input  in_3,
  input  Clock,
  input  Reset,
  input  in_6,
  input  in_7,
  input  in_8,
  input  in_9,
  input  in_10,
  input  in_11,
  input  in_12,
  input  in_13,
  input  in_14,
  input  in_15,
  input  in_16,
  input  in_17,
  input  in_18,
  input  in_19,
  input  in_20,
  input  in_21,
  input  in_22,
  input  in_23,
  input  in_24,
  input  in_25,
  input  in_26,
  input  in_27,
  input  in_28,
  input  in_29,
  input  in_30,
  input  in_31,
  input  in_32,
  input  in_33,
  input  in_34,
  output [31:0] out_35,
  output [31:0] out_36,
  output [31:0] out_37,
  output [31:0] out_38,
  output [31:0] out_39,
  output [31:0] out_40,
  output [31:0] out_41,
  output [31:0] out_42,
  output [31:0] out_43,
  output [31:0] out_44,
  output [31:0] out_45,
  output [31:0] out_46,
  output [31:0] out_47,
  output [31:0] out_48,
  output [31:0] out_49,
  output [31:0] out_50,
  output [31:0] out_51,
  output [31:0] out_52,
  output [31:0] out_53,
  output [31:0] out_54,
  output [31:0] out_55,
  output [31:0] out_56,
  output [31:0] out_57,
  output [31:0] out_58,
  output [31:0] out_59,
  output [31:0] out_60,
  output [31:0] out_61,
  output [31:0] out_62,
  output [31:0] out_63,
  output [31:0] out_64,
  output [31:0] out_65
);

  Register #(.width(32)) register_1 (.D({32{1'b0}}), .en(in_1), .Q(out_35), .clk(Clock), .clr(Reset));
  Register #(.width(32)) register_2 (.D(A), .en(in_3), .Q(out_36), .clk(Clock), .clr(Reset));
  Register #(.width(32)) register_3 (.D(A), .en(in_6), .Q(out_37), .clk(Clock), .clr(Reset));
  Register #(.width(32)) register_4 (.D(A), .en(in_7), .Q(out_38), .clk(Clock), .clr(Reset));
  Register #(.width(32)) register_5 (.D(A), .en(in_8), .Q(out_39), .clk(Clock), .clr(Reset));
  Register #(.width(32)) register_6 (.D(A), .en(in_9), .Q(out_40), .clk(Clock), .clr(Reset));
  Register #(.width(32)) register_7 (.D(A), .en(in_10), .Q(out_41), .clk(Clock), .clr(Reset));
  Register #(.width(32)) register_8 (.D(A), .en(in_11), .Q(out_42), .clk(Clock), .clr(Reset));
  Register #(.width(32)) register_9 (.D(A), .en(in_12), .Q(out_43), .clk(Clock), .clr(Reset));
  Register #(.width(32)) register_10 (.D(A), .en(in_13), .Q(out_44), .clk(Clock), .clr(Reset));
  Register #(.width(32)) register_11 (.D(A), .en(in_14), .Q(out_45), .clk(Clock), .clr(Reset));
  Register #(.width(32)) register_12 (.D(A), .en(in_15), .Q(out_46), .clk(Clock), .clr(Reset));
  Register #(.width(32)) register_13 (.D(A), .en(in_16), .Q(out_47), .clk(Clock), .clr(Reset));
  Register #(.width(32)) register_14 (.D(A), .en(in_17), .Q(out_48), .clk(Clock), .clr(Reset));
  Register #(.width(32)) register_15 (.D(A), .en(in_18), .Q(out_49), .clk(Clock), .clr(Reset));
  Register #(.width(32)) register_16 (.D(A), .en(in_19), .Q(out_50), .clk(Clock), .clr(Reset));
  Register #(.width(32)) register_17 (.D(A), .en(in_20), .Q(out_51), .clk(Clock), .clr(Reset));
  Register #(.width(32)) register_18 (.D(A), .en(in_21), .Q(out_52), .clk(Clock), .clr(Reset));
  Register #(.width(32)) register_19 (.D(A), .en(in_22), .Q(out_53), .clk(Clock), .clr(Reset));
  Register #(.width(32)) register_20 (.D(A), .en(in_23), .Q(out_54), .clk(Clock), .clr(Reset));
  Register #(.width(32)) register_21 (.D(A), .en(in_24), .Q(out_55), .clk(Clock), .clr(Reset));
  Register #(.width(32)) register_22 (.D(A), .en(in_25), .Q(out_56), .clk(Clock), .clr(Reset));
  Register #(.width(32)) register_23 (.D(A), .en(in_26), .Q(out_57), .clk(Clock), .clr(Reset));
  Register #(.width(32)) register_24 (.D(A), .en(in_27), .Q(out_58), .clk(Clock), .clr(Reset));
  Register #(.width(32)) register_25 (.D(A), .en(in_28), .Q(out_59), .clk(Clock), .clr(Reset));
  Register #(.width(32)) register_26 (.D(A), .en(in_29), .Q(out_60), .clk(Clock), .clr(Reset));
  Register #(.width(32)) register_27 (.D(A), .en(in_30), .Q(out_61), .clk(Clock), .clr(Reset));
  Register #(.width(32)) register_28 (.D(A), .en(in_31), .Q(out_62), .clk(Clock), .clr(Reset));
  Register #(.width(32)) register_29 (.D(A), .en(in_32), .Q(out_63), .clk(Clock), .clr(Reset));
  Register #(.width(32)) register_30 (.D(A), .en(in_33), .Q(out_64), .clk(Clock), .clr(Reset));
  Register #(.width(32)) register_31 (.D(A), .en(in_34), .Q(out_65), .clk(Clock), .clr(Reset));

  // Other names for the same wires on the sheet: CLK = Clock
endmodule
