// Logisim project cu (3).circ as structural Verilog: 1 circuit, main circuit rw
module rw (
  input  in_1,
  input  in_2,
  input  in_3,
  input  in_4,
  input  in_5,
  input  in_6,
  input  in_7,
  input  in_8,
  input  in_9,
  input  in_10,
  input  in_11,
  input  in_12,
  input  in_13,
  input  in_14,
  input  in_15,
  input  in_16,
  input  in_17,
  input  in_18,
  input  in_19,
  input  in_20,
  input  in_21,
  input  in_22,
  input  in_23,
  input  in_24,
  input  in_25,
  input  in_26,
  input  in_27,
  input  in_28,
  input  in_29,
  input  in_30,
  input  in_31,
  input  in_32,
  input  RW,
  output out_34,
  output out_35,
  output out_36,
  output out_37,
  output out_38,
  output out_39,
  output out_40,
  output out_41,
  output out_42,
  output out_43,
  output out_44,
  output out_45,
  output out_46,
  output out_47,
  output out_48,
  output out_49,
  output out_50,
  output out_51,
  output out_52,
  output out_53,
  output out_54,
  output out_55,
  output out_56,
  output out_57,
  output out_58,
  output out_59,
  output out_60,
  output out_61,
  output out_62,
  output out_63,
  output out_64,
  output out_65
);

  and and_1 (out_34, in_1, RW);
  and and_2 (out_38, in_5, RW);
  and and_3 (out_42, in_9, RW);
  and and_4 (out_46, in_13, RW);
  and and_5 (out_50, in_17, RW);
  and and_6 (out_54, in_21, RW);
  and and_7 (out_58, in_25, RW);
  and and_8 (out_62, in_29, RW);
  and and_9 (out_35, in_2, RW);
  and and_10 (out_39, in_6, RW);
  and and_11 (out_43, in_10, RW);
  and and_12 (out_47, in_14, RW);
  and and_13 (out_51, in_18, RW);
  and and_14 (out_55, in_22, RW);
  and and_15 (out_59, in_26, RW);
  and and_16 (out_63, in_30, RW);
  and and_17 (out_36, in_3, RW);
  and and_18 (out_40, in_7, RW);
  and and_19 (out_44, in_11, RW);
  and and_20 (out_48, in_15, RW);
  and and_21 (out_52, in_19, RW);
  and and_22 (out_56, in_23, RW);
  and and_23 (out_60, in_27, RW);
  and and_24 (out_64, in_31, RW);
  and and_25 (out_37, in_4, RW);
  and and_26 (out_41, in_8, RW);
  and and_27 (out_45, in_12, RW);
  and and_28 (out_49, in_16, RW);
  and and_29 (out_53, in_20, RW);
  and and_30 (out_57, in_24, RW);
  and and_31 (out_61, in_28, RW);
  and and_32 (out_65, in_32, RW);
endmodule
