// Logisim project cu (4).circ as structural Verilog: 1 circuit, main circuit div
module div (
  input  [31:0] A,
  input  [31:0] B,
  output [31:0] Lo,
  output [31:0] Hi
);

  wire comparator_1_lt, xor_1_out, xor_2_out;
  wire [31:0] adder_1_out, adder_2_out, adder_3_out, adder_4_out, divider_1_out, divider_1_rem,
       multiplexer_1_out, multiplexer_2_out, multiplexer_3_out, multiplier_1_out, not_1_out, not_2_out,
       not_3_out, not_4_out;

  assign not_1_out = ~A;  // NOT_Gate not_1, 32 bits wide
  Adder #(.width(32)) adder_1 (.a(not_1_out), .b(32'h1), .out(adder_1_out));  // open: cin, cout
  assign not_2_out = ~B;  // NOT_Gate not_2, 32 bits wide
  Adder #(.width(32)) adder_2 (.a(not_2_out), .b(32'h1), .out(adder_2_out));  // open: cin, cout
  Multiplexer #(.width(32), .enable("false")) multiplexer_1 (
    .in0(A), .in1(adder_1_out), .out(multiplexer_1_out), .sel(A[31]));
  Multiplexer #(.width(32), .enable("false")) multiplexer_2 (
    .in0(B), .in1(adder_2_out), .out(multiplexer_2_out), .sel(B[31]));
  Divider #(.width(32)) divider_1 (
    .a(multiplexer_1_out), .b(multiplexer_2_out), .out(divider_1_out), .rem(divider_1_rem));  // open: upper
  assign not_3_out = ~divider_1_rem;  // NOT_Gate not_3, 32 bits wide
  xor xor_1 (xor_1_out, B[31], A[31]);
  Adder #(.width(32)) adder_3 (.a(not_3_out), .b(32'h1), .out(adder_3_out));  // open: cin, cout
  assign not_4_out = ~divider_1_out;  // NOT_Gate not_4, 32 bits wide
  Adder #(.width(32)) adder_4 (.a(not_4_out), .b(32'h1), .out(adder_4_out));  // open: cin, cout
  Multiplexer #(.width(32), .enable("false")) multiplexer_3 (
    .in0(divider_1_rem), .in1(adder_3_out), .out(multiplexer_3_out), .sel(xor_1_out));
  Multiplexer #(.width(32), .enable("false")) multiplexer_4 (
    .in0(divider_1_out), .in1(adder_4_out), .out(Lo), .sel(xor_2_out));
  xor xor_2 (xor_2_out, B[31], A[31]);
  Multiplier #(.width(32)) multiplier_1 (
    .a(multiplexer_3_out), .b({32{1'b1}}), .out(multiplier_1_out));  // open: cin, cout
  Comparator #(.width(32)) comparator_1 (.a(multiplexer_3_out), .b({32{1'b0}}), .lt(comparator_1_lt));  // open: gt, eq
  Multiplexer #(.width(32), .enable("false")) multiplexer_5 (
    .in0(multiplexer_3_out), .in1(multiplier_1_out), .out(Hi), .sel(comparator_1_lt));

  // Other names for the same wires on the sheet: S_prime_prime = B[31]; S_prime = A[31]

  // Notes on the sheet:
  //   INPUT:
  //   OUTPUT:
endmodule
