// Logisim project cu (5).circ as structural Verilog: 1 circuit, main circuit mulu
module mulu (
  input  [31:0] A,
  input  [31:0] B,
  output [31:0] Hi,
  output [31:0] Lo
);

  wire adder_1_cout, adder_2_cout, adder_3_cout, adder_4_cout, adder_5_cout, adder_6_cout, adder_7_cout,
       adder_9_cout, adder_10_cout, adder_11_cout, adder_12_cout, adder_13_cout, adder_14_cout,
       adder_15_cout, adder_17_cout, adder_18_cout, adder_19_cout, adder_20_cout, adder_21_cout,
       adder_22_cout, adder_23_cout, adder_25_cout, adder_26_cout, adder_27_cout, adder_28_cout,
       adder_29_cout, adder_30_cout, adder_31_cout, Carry7, Carry15, Carry23;
  wire [30:0] adder_1_out, adder_2_out, adder_3_out, adder_4_out, adder_5_out, adder_6_out, adder_7_out,
       adder_9_out, adder_10_out, adder_11_out, adder_12_out, adder_13_out, adder_14_out, adder_15_out,
       adder_17_out, adder_18_out, adder_19_out, adder_20_out, adder_21_out, adder_22_out, adder_23_out,
       adder_25_out, adder_26_out, adder_27_out, adder_28_out, adder_29_out, adder_30_out, adder_31_out;
  wire [31:0] _0, _1, _2, _3, _4, _5, _6, _7, _8, _9, _10, _11, _12, _13, _14, _15, _16, _17, _18, _19, _20,
       _21, _22, _23, _24, _25, _26, _27, _28, _29, _30, _31, and_1_out, and_2_out, and_3_out, and_4_out,
       and_5_out, and_6_out, and_7_out, and_8_out, and_9_out, and_10_out, and_11_out, and_12_out, and_13_out,
       and_14_out, and_15_out, and_16_out, and_17_out, and_18_out, and_19_out, and_20_out, and_21_out,
       and_22_out, and_23_out, and_24_out, and_25_out, and_26_out, and_27_out, and_28_out, and_29_out,
       and_30_out, and_31_out, and_32_out;
  wire [31:1] adder_8_out, adder_16_out, adder_24_out;

  assign and_1_out = A & _0;  // AND_Gate and_1, 32 bits wide
  assign and_2_out = A & _1;  // AND_Gate and_2, 32 bits wide
  assign and_3_out = A & _2;  // AND_Gate and_3, 32 bits wide
  assign and_4_out = A & _3;  // AND_Gate and_4, 32 bits wide
  assign and_5_out = A & _4;  // AND_Gate and_5, 32 bits wide
  assign and_6_out = A & _5;  // AND_Gate and_6, 32 bits wide
  assign and_7_out = A & _6;  // AND_Gate and_7, 32 bits wide
  assign and_8_out = A & _7;  // AND_Gate and_8, 32 bits wide
  Adder #(.width(32)) adder_1 (
    .a({32{1'b0}}), .b(and_1_out), .out({adder_1_out, Lo[0]}), .cout(adder_1_cout));  // open: cin
  Adder #(.width(32)) adder_2 (
    .a({1'b0, adder_1_out}), .b(and_2_out), .out({adder_2_out, Lo[1]}), .cin(adder_1_cout),
    .cout(adder_2_cout));
  Adder #(.width(32)) adder_3 (
    .a({1'b0, adder_2_out}), .b(and_3_out), .out({adder_3_out, Lo[2]}), .cin(adder_2_cout),
    .cout(adder_3_cout));
  Adder #(.width(32)) adder_4 (
    .a({1'b0, adder_3_out}), .b(and_4_out), .out({adder_4_out, Lo[3]}), .cin(adder_3_cout),
    .cout(adder_4_cout));
  Adder #(.width(32)) adder_5 (
    .a({1'b0, adder_4_out}), .b(and_5_out), .out({adder_5_out, Lo[4]}), .cin(adder_4_cout),
    .cout(adder_5_cout));
  Adder #(.width(32)) adder_6 (
    .a({1'b0, adder_5_out}), .b(and_6_out), .out({adder_6_out, Lo[5]}), .cin(adder_5_cout),
    .cout(adder_6_cout));
  Adder #(.width(32)) adder_7 (
    .a({1'b0, adder_6_out}), .b(and_7_out), .out({adder_7_out, Lo[6]}), .cin(adder_6_cout),
    .cout(adder_7_cout));
  Adder #(.width(32)) adder_8 (
    .a({1'b0, adder_7_out}), .b(and_8_out), .out({adder_8_out, Lo[7]}), .cin(adder_7_cout), .cout(Carry7));
  assign _0 = {{31{B[0]}}, B[0]};  // Bit_Extender bit_extender_1
  assign _1 = {{31{B[1]}}, B[1]};  // Bit_Extender bit_extender_2
  assign _2 = {{31{B[2]}}, B[2]};  // Bit_Extender bit_extender_3
  assign _3 = {{31{B[3]}}, B[3]};  // Bit_Extender bit_extender_4
  assign _4 = {{31{B[4]}}, B[4]};  // Bit_Extender bit_extender_5
  assign _5 = {{31{B[5]}}, B[5]};  // Bit_Extender bit_extender_6
  assign _6 = {{31{B[6]}}, B[6]};  // Bit_Extender bit_extender_7
  assign _7 = {{31{B[7]}}, B[7]};  // Bit_Extender bit_extender_8
  assign and_9_out = A & _8;  // AND_Gate and_9, 32 bits wide
  assign and_10_out = A & _9;  // AND_Gate and_10, 32 bits wide
  assign and_11_out = A & _10;  // AND_Gate and_11, 32 bits wide
  assign and_12_out = A & _11;  // AND_Gate and_12, 32 bits wide
  assign and_13_out = A & _12;  // AND_Gate and_13, 32 bits wide
  assign and_14_out = A & _13;  // AND_Gate and_14, 32 bits wide
  assign and_15_out = A & _14;  // AND_Gate and_15, 32 bits wide
  assign and_16_out = A & _15;  // AND_Gate and_16, 32 bits wide
  Adder #(.width(32)) adder_9 (
    .a({1'b0, adder_8_out}), .b(and_9_out), .out({adder_9_out, Lo[8]}), .cin(Carry7), .cout(adder_9_cout));
  Adder #(.width(32)) adder_10 (
    .a({1'b0, adder_9_out}), .b(and_10_out), .out({adder_10_out, Lo[9]}), .cin(adder_9_cout),
    .cout(adder_10_cout));
  Adder #(.width(32)) adder_11 (
    .a({1'b0, adder_10_out}), .b(and_11_out), .out({adder_11_out, Lo[10]}), .cin(adder_10_cout),
    .cout(adder_11_cout));
  Adder #(.width(32)) adder_12 (
    .a({1'b0, adder_11_out}), .b(and_12_out), .out({adder_12_out, Lo[11]}), .cin(adder_11_cout),
    .cout(adder_12_cout));
  Adder #(.width(32)) adder_13 (
    .a({1'b0, adder_12_out}), .b(and_13_out), .out({adder_13_out, Lo[12]}), .cin(adder_12_cout),
    .cout(adder_13_cout));
  Adder #(.width(32)) adder_14 (
    .a({1'b0, adder_13_out}), .b(and_14_out), .out({adder_14_out, Lo[13]}), .cin(adder_13_cout),
    .cout(adder_14_cout));
  Adder #(.width(32)) adder_15 (
    .a({1'b0, adder_14_out}), .b(and_15_out), .out({adder_15_out, Lo[14]}), .cin(adder_14_cout),
    .cout(adder_15_cout));
  Adder #(.width(32)) adder_16 (
    .a({1'b0, adder_15_out}), .b(and_16_out), .out({adder_16_out, Lo[15]}), .cin(adder_15_cout),
    .cout(Carry15));
  assign _8 = {{31{B[8]}}, B[8]};  // Bit_Extender bit_extender_9
  assign _9 = {{31{B[9]}}, B[9]};  // Bit_Extender bit_extender_10
  assign _10 = {{31{B[10]}}, B[10]};  // Bit_Extender bit_extender_11
  assign _11 = {{31{B[11]}}, B[11]};  // Bit_Extender bit_extender_12
  assign _12 = {{31{B[12]}}, B[12]};  // Bit_Extender bit_extender_13
  assign _13 = {{31{B[13]}}, B[13]};  // Bit_Extender bit_extender_14
  assign _14 = {{31{B[14]}}, B[14]};  // Bit_Extender bit_extender_15
  assign _15 = {{31{B[15]}}, B[15]};  // Bit_Extender bit_extender_16
  assign and_17_out = A & _16;  // AND_Gate and_17, 32 bits wide
  assign and_18_out = A & _17;  // AND_Gate and_18, 32 bits wide
  assign and_19_out = A & _18;  // AND_Gate and_19, 32 bits wide
  assign and_20_out = A & _19;  // AND_Gate and_20, 32 bits wide
  assign and_21_out = A & _20;  // AND_Gate and_21, 32 bits wide
  assign and_22_out = A & _21;  // AND_Gate and_22, 32 bits wide
  assign and_23_out = A & _22;  // AND_Gate and_23, 32 bits wide
  assign and_24_out = A & _23;  // AND_Gate and_24, 32 bits wide
  assign _16 = {{31{B[16]}}, B[16]};  // Bit_Extender bit_extender_17
  assign _17 = {{31{B[17]}}, B[17]};  // Bit_Extender bit_extender_18
  assign _18 = {{31{B[18]}}, B[18]};  // Bit_Extender bit_extender_19
  assign _19 = {{31{B[19]}}, B[19]};  // Bit_Extender bit_extender_20
  assign _20 = {{31{B[20]}}, B[20]};  // Bit_Extender bit_extender_21
  assign _21 = {{31{B[21]}}, B[21]};  // Bit_Extender bit_extender_22
  assign _22 = {{31{B[22]}}, B[22]};  // Bit_Extender bit_extender_23
  assign _23 = {{31{B[23]}}, B[23]};  // Bit_Extender bit_extender_24
  Adder #(.width(32)) adder_17 (
    .a({1'b0, adder_16_out}), .b(and_17_out), .out({adder_17_out, Lo[16]}), .cin(Carry15),
    .cout(adder_17_cout));
  Adder #(.width(32)) adder_18 (
    .a({1'b0, adder_17_out}), .b(and_18_out), .out({adder_18_out, Lo[17]}), .cin(adder_17_cout),
    .cout(adder_18_cout));
  Adder #(.width(32)) adder_19 (
    .a({1'b0, adder_18_out}), .b(and_19_out), .out({adder_19_out, Lo[18]}), .cin(adder_18_cout),
    .cout(adder_19_cout));
  Adder #(.width(32)) adder_20 (
    .a({1'b0, adder_19_out}), .b(and_20_out), .out({adder_20_out, Lo[19]}), .cin(adder_19_cout),
    .cout(adder_20_cout));
  Adder #(.width(32)) adder_21 (
    .a({1'b0, adder_20_out}), .b(and_21_out), .out({adder_21_out, Lo[20]}), .cin(adder_20_cout),
    .cout(adder_21_cout));
  Adder #(.width(32)) adder_22 (
    .a({1'b0, adder_21_out}), .b(and_22_out), .out({adder_22_out, Lo[21]}), .cin(adder_21_cout),
    .cout(adder_22_cout));
  Adder #(.width(32)) adder_23 (
    .a({1'b0, adder_22_out}), .b(and_23_out), .out({adder_23_out, Lo[22]}), .cin(adder_22_cout),
    .cout(adder_23_cout));
  Adder #(.width(32)) adder_24 (
    .a({1'b0, adder_23_out}), .b(and_24_out), .out({adder_24_out, Lo[23]}), .cin(adder_23_cout),
    .cout(Carry23));
  assign _24 = {{31{B[24]}}, B[24]};  // Bit_Extender bit_extender_25
  assign _25 = {{31{B[25]}}, B[25]};  // Bit_Extender bit_extender_26
  assign _26 = {{31{B[26]}}, B[26]};  // Bit_Extender bit_extender_27
  assign _27 = {{31{B[27]}}, B[27]};  // Bit_Extender bit_extender_28
  assign _28 = {{31{B[28]}}, B[28]};  // Bit_Extender bit_extender_29
  assign _29 = {{31{B[29]}}, B[29]};  // Bit_Extender bit_extender_30
  assign _30 = {{31{B[30]}}, B[30]};  // Bit_Extender bit_extender_31
  assign _31 = {{31{B[31]}}, B[31]};  // Bit_Extender bit_extender_32
  assign and_25_out = A & _24;  // AND_Gate and_25, 32 bits wide
  assign and_26_out = A & _25;  // AND_Gate and_26, 32 bits wide
  assign and_27_out = A & _26;  // AND_Gate and_27, 32 bits wide
  assign and_28_out = A & _27;  // AND_Gate and_28, 32 bits wide
  assign and_29_out = A & _28;  // AND_Gate and_29, 32 bits wide
  assign and_30_out = A & _29;  // AND_Gate and_30, 32 bits wide
  assign and_31_out = A & _30;  // AND_Gate and_31, 32 bits wide
  assign and_32_out = A & _31;  // AND_Gate and_32, 32 bits wide
  Adder #(.width(32)) adder_25 (
    .a({1'b0, adder_24_out}), .b(and_25_out), .out({adder_25_out, Lo[24]}), .cin(Carry23),
    .cout(adder_25_cout));
  Adder #(.width(32)) adder_26 (
    .a({1'b0, adder_25_out}), .b(and_26_out), .out({adder_26_out, Lo[25]}), .cin(adder_25_cout),
    .cout(adder_26_cout));
  Adder #(.width(32)) adder_27 (
    .a({1'b0, adder_26_out}), .b(and_27_out), .out({adder_27_out, Lo[26]}), .cin(adder_26_cout),
    .cout(adder_27_cout));
  Adder #(.width(32)) adder_28 (
    .a({1'b0, adder_27_out}), .b(and_28_out), .out({adder_28_out, Lo[27]}), .cin(adder_27_cout),
    .cout(adder_28_cout));
  Adder #(.width(32)) adder_29 (
    .a({1'b0, adder_28_out}), .b(and_29_out), .out({adder_29_out, Lo[28]}), .cin(adder_28_cout),
    .cout(adder_29_cout));
  Adder #(.width(32)) adder_30 (
    .a({1'b0, adder_29_out}), .b(and_30_out), .out({adder_30_out, Lo[29]}), .cin(adder_29_cout),
    .cout(adder_30_cout));
  Adder #(.width(32)) adder_31 (
    .a({1'b0, adder_30_out}), .b(and_31_out), .out({adder_31_out, Lo[30]}), .cin(adder_30_cout),
    .cout(adder_31_cout));
  Adder #(.width(32)) adder_32 (
    .a({1'b0, adder_31_out}), .b(and_32_out), .out({Hi[30:0], Lo[31]}), .cin(adder_31_cout), .cout(Hi[31]));

  // Other names for the same wires on the sheet: Carry21 = Hi[31]; O0 = Lo[0]; O1 = Lo[1]; O2 = Lo[2]; O3 = Lo[3];
  //   O4 = Lo[4]; O5 = Lo[5]; O6 = Lo[6]; O7 = Lo[7]; O8 = Lo[8]; O9 = Lo[9]; O10 = Lo[10]; O11 = Lo[11];
  //   O12 = Lo[12]; O13 = Lo[13]; O14 = Lo[14]; O15 = Lo[15]; O16 = Lo[16]; O17 = Lo[17]; O18 = Lo[18]; O19 = Lo[19];
  //   O20 = Lo[20]; O21 = Lo[21]; O22 = Lo[22]; O23 = Lo[23]; O24 = Lo[24]; O25 = Lo[25]; O26 = Lo[26]; O27 = Lo[27];
  //   O28 = Lo[28]; O29 = Lo[29]; O30 = Lo[30]; O31 = Lo[31]

  // Notes on the sheet:
  //   INPUT:
  //   OUTPUT:
endmodule
