// Logisim project cu (6).circ as structural Verilog
module CU (
  input  nop,
  input  \and ,
  input  xori,
  input  bltz,
  input  add,
  input  \or ,
  input  lw,
  input  j,
  input  sub,
  input  \nor ,
  input  sw,
  input  jr,
  input  mul,
  input  \xor ,
  input  pop,
  input  mfhi,
  input  mulu,
  input  addi,
  input  push,
  input  mflo,
  input  div,
  input  slti,
  input  beq,
  input  halt,
  input  divu,
  input  sltiu,
  input  bne,
  input  tty,
  input  slt,
  input  andi,
  input  blez,
  input  rnd,
  input  sltu,
  input  ori,
  input  bgtz,
  input  kbd,
  input  Reset,
  input  Clock,
  input  SP_0,
  input  RT__0,
  input  WT__0,
  input  First_Instruction,
  input  KBD_Avalaible,
  output ALUSB,
  output [2:0] Selector_Data_Input,
  output [1:0] Stack_Point_Selector,
  output CURW,
  output [2:0] Branch_Control_Selector,
  output Enabled_PC,
  output CS,
  output [1:0] Memory_Manager_Selector,
  output SRT,
  output SWT,
  output minus_RW,
  output Enable_Inst,
  output KBD_Enable,
  output TTY_Enable
);

  wire ALUSB0, ALUSB1, BCS0_0, BCS0_1, BCS0_2, BCS1_0, BCS2_0, demultiplexer_1_out0, demultiplexer_1_out1,
       demultiplexer_2_out0, demultiplexer_2_out1, demultiplexer_3_out1, demultiplexer_4_out0,
       demultiplexer_4_out1, demultiplexer_5_out0, demultiplexer_6_out1, demultiplexer_7_out0,
       demultiplexer_7_out1, demultiplexer_9_out0, demultiplexer_9_out1, demultiplexer_11_out0,
       demultiplexer_11_out1, demultiplexer_12_out0, demultiplexer_12_out1, demultiplexer_13_out0,
       demultiplexer_14_out0, demultiplexer_14_out1, demultiplexer_15_out1, demultiplexer_16_out0,
       demultiplexer_16_out1, demultiplexer_17_out0, demultiplexer_17_out1, demultiplexer_18_out0,
       demultiplexer_18_out1, demultiplexer_19_out0, demultiplexer_19_out1, demultiplexer_20_out1,
       demultiplexer_21_out1, demultiplexer_22_out0, demultiplexer_22_out1, demultiplexer_23_out0,
       demultiplexer_23_out1, demultiplexer_24_out0, demultiplexer_24_out1, demultiplexer_25_out0,
       demultiplexer_25_out1, demultiplexer_27_out0, demultiplexer_27_out1, demultiplexer_28_out1,
       demultiplexer_29_out1, demultiplexer_30_out0, demultiplexer_31_out0, demultiplexer_33_out1,
       demultiplexer_37_out1, demultiplexer_38_out1, demultiplexer_41_out0, demultiplexer_41_out1,
       demultiplexer_42_out0, demultiplexer_43_out0, demultiplexer_44_out1, demultiplexer_45_out0,
       demultiplexer_45_out1, demultiplexer_46_out0, demultiplexer_46_out1, demultiplexer_47_out0,
       demultiplexer_47_out1, demultiplexer_48_out1, demultiplexer_49_out1, demultiplexer_50_out1,
       demultiplexer_51_out1, demultiplexer_52_out1, En_Inst0, En_Inst1, En_PC5, End_2_q, End_5_q, End_6_q,
       End_7_q, End_8_q, end_ALU, End_BCU, End_Instruction_q, end_MM, End_q, End_RF, End_RT, End_RT_2_q,
       End_RT_q, End_WT, End_WT_2_q, End_WT_q, F, First_Instruction_q, Idle_2_q, Idle_4_q, Idle_5_q,
       Idle_6_q, Idle_7_q, Idle_8_q, Idle_9_q, minus_RW1, MMS0_0, MMS0_2, MMS1_1, not_2_out, not_3_out,
       not_4_out, not_5_out, not_6_out, not_7_out, not_8_out, not_9_out, not_10_out, not_11_out, not_12_out,
       not_13_out, not_14_out, not_15_out, o0, o1, o2, o3, o4, o5, o6, o7, o8, o9, o10, or_1_out, or_2_out,
       or_3_out, or_6_out, or_7_out, or_8_out, or_10_out, or_11_out, or_15_out, or_16_out, or_17_out,
       or_18_out, or_23_out, or_25_out, or_26_out, or_27_out, or_28_out, or_29_out, or_30_out, or_31_out,
       or_32_out, or_33_out, or_34_out, or_35_out, or_36_out, or_37_out, or_38_out, or_39_out, or_40_out,
       or_41_out, or_42_out, or_43_out, or_44_out, or_45_out, or_46_out, or_47_out, or_48_out, or_49_out,
       or_51_out, or_55_out, or_56_out, or_58_out, PC_q, Push_Write_Time_q, Read_Time_2_q, rst, RW0, RW1,
       SDI0_0, SDI0_1, SRT0, SRT1, SRT2, SRT3, SSP0_0, start, Update_Values_q, wait_branch, Wait_MM_2_q,
       Wait_MM_3_q, Wait_MM_4_q, Wait_MM_5_q, Wait_MM_q, wait_rf, Wr, Write_Time_q;

  or or_1 (or_1_out, end_MM, Reset);
  or or_2 (or_2_out, Reset, halt);
  D_Flip_Flop Idle (.clk(Clock), .D(Idle_2_q), .Q(start));  // open: Qn, preset, en, reset
  D_Flip_Flop Idle_2 (.clk(Clock), .D(or_1_out), .Q(Idle_2_q));  // open: Qn, preset, en, reset
  D_Flip_Flop Idle_3 (.clk(Clock), .D(or_2_out), .Q(rst));  // open: Qn, preset, en, reset
  or or_3 (or_3_out, demultiplexer_1_out0, demultiplexer_50_out1);
  or or_4 (Memory_Manager_Selector[0], MMS0_0, MMS0_2, ALUSB1);
  or or_5 (Memory_Manager_Selector[1], minus_RW1, MMS1_1);
  D_Flip_Flop Idle_4 (.clk(Clock), .D(or_6_out), .Q(Idle_4_q), .preset(rst));  // open: Qn, en, reset
  or or_6 (or_6_out, demultiplexer_2_out0, demultiplexer_52_out1);
  or or_7 (or_7_out, demultiplexer_4_out0, demultiplexer_51_out1);
  not not_1 (CS, demultiplexer_1_out0);
  Demultiplexer #(.enable("false")) demultiplexer_1 (
    .out0(demultiplexer_1_out0), .out1(demultiplexer_1_out1), .in(Idle_5_q), .sel(start));
  D_Flip_Flop Idle_5 (.clk(Clock), .D(or_3_out), .Q(Idle_5_q), .preset(rst));  // open: Qn, en, reset
  Demultiplexer #(.enable("false")) demultiplexer_2 (
    .out0(demultiplexer_2_out0), .out1(demultiplexer_2_out1), .in(Idle_4_q), .sel(start));
  Demultiplexer #(.enable("false")) demultiplexer_3 (.out0(o7), .out1(demultiplexer_3_out1), .in(F), .sel(not_2_out));
  or or_8 (or_8_out, add, sub, mul, mulu, div, divu, slt, sltu, \and , \or , \nor , \xor , addi, slti, sltiu, andi, ori, xori);
  not not_2 (not_2_out, or_8_out);
  D_Flip_Flop Idle_6 (.clk(Clock), .D(or_7_out), .Q(Idle_6_q), .preset(rst));  // open: Qn, en, reset
  Demultiplexer #(.enable("false")) demultiplexer_4 (
    .out0(demultiplexer_4_out0), .out1(demultiplexer_4_out1), .in(Idle_6_q), .sel(start));
  Demultiplexer #(.enable("false")) demultiplexer_5 (
    .out0(demultiplexer_5_out0), .out1(En_Inst1), .in(demultiplexer_1_out1), .sel(not_3_out));
  not not_3 (not_3_out, First_Instruction);
  or or_9 (Enable_Inst, En_Inst0, En_Inst1);
  D_Flip_Flop Wait_MM (.clk(Clock), .D(or_10_out), .Q(Wait_MM_q), .reset(rst));  // open: Qn, preset, en
  or or_10 (or_10_out, demultiplexer_7_out0, demultiplexer_2_out1);
  Demultiplexer #(.enable("false")) demultiplexer_6 (
    .out0(o8), .out1(demultiplexer_6_out1), .in(demultiplexer_3_out1), .sel(not_4_out));
  not not_4 (not_4_out, rnd);
  or or_11 (or_11_out, demultiplexer_9_out0, demultiplexer_4_out1);
  or or_12 (Branch_Control_Selector[0], BCS0_0, BCS0_2, BCS0_1);
  or or_13 (Branch_Control_Selector[1], BCS1_0, BCS0_1);
  or or_14 (Branch_Control_Selector[2], BCS2_0, BCS0_2);
  D_Flip_Flop u_First_Instruction (
    .clk(Clock), .D(or_15_out), .Q(First_Instruction_q), .reset(rst));  // open: Qn, preset, en
  or or_15 (or_15_out, SRT0, demultiplexer_5_out0);
  or or_16 (or_16_out, En_Inst0, En_Inst1);
  or or_17 (or_17_out, demultiplexer_11_out0, demultiplexer_45_out1);
  or or_18 (or_18_out, demultiplexer_12_out0, demultiplexer_46_out1);
  Demultiplexer #(.enable("false")) demultiplexer_7 (
    .out0(demultiplexer_7_out0), .out1(demultiplexer_7_out1), .in(Wait_MM_q), .sel(wait_rf));
  Demultiplexer #(.enable("false")) demultiplexer_8 (
    .out0(o9), .out1(o10), .in(demultiplexer_6_out1), .sel(KBD_Avalaible));
  D_Flip_Flop Wait_MM_2 (.clk(Clock), .D(or_11_out), .Q(Wait_MM_2_q), .reset(rst));  // open: Qn, preset, en
  Demultiplexer #(.enable("false")) demultiplexer_9 (
    .out0(demultiplexer_9_out0), .out1(demultiplexer_9_out1), .in(Wait_MM_2_q), .sel(wait_branch));
  Demultiplexer #(.enable("false")) demultiplexer_10 (
    .out0(SRT0), .out1(En_Inst0), .in(First_Instruction_q), .sel(RT__0));
  D_Flip_Flop Current_Instruction (.clk(Clock), .D(or_16_out), .Q(wait_rf), .reset(rst));  // open: Qn, preset, en
  or or_19 (Wr, sw, push);
  or or_20 (SRT, SRT0, SRT1, SRT2, SRT3);
  or or_21 (SWT, ALUSB1, minus_RW1);
  or or_22 (minus_RW, ALUSB1, minus_RW1);
  Demultiplexer #(.enable("false")) demultiplexer_11 (
    .out0(demultiplexer_11_out0), .out1(demultiplexer_11_out1), .in(Idle_7_q), .sel(start));
  D_Flip_Flop Idle_7 (.clk(Clock), .D(or_17_out), .Q(Idle_7_q), .preset(rst));  // open: Qn, en, reset
  D_Flip_Flop Idle_8 (.clk(Clock), .D(or_18_out), .Q(Idle_8_q), .preset(rst));  // open: Qn, en, reset
  Demultiplexer #(.enable("false")) demultiplexer_12 (
    .out0(demultiplexer_12_out0), .out1(demultiplexer_12_out1), .in(Idle_8_q), .sel(start));
  or or_23 (or_23_out, add, sub, mul, mulu, div, divu, slt, sltu, \and , \or , \nor , \xor , beq, bne, blez, bgtz, bltz);
  Demultiplexer #(.enable("false")) demultiplexer_13 (
    .out0(demultiplexer_13_out0), .out1(o1), .in(demultiplexer_14_out0), .sel(SP_0));
  Demultiplexer #(.enable("false")) demultiplexer_14 (
    .out0(demultiplexer_14_out0), .out1(demultiplexer_14_out1), .in(demultiplexer_7_out1), .sel(not_5_out));
  not not_5 (not_5_out, pop);
  Demultiplexer #(.enable("false")) demultiplexer_15 (
    .out0(BCS0_0), .out1(demultiplexer_15_out1), .in(demultiplexer_9_out1), .sel(not_6_out));
  not not_6 (not_6_out, beq);
  // OR_Gate or_24 has open pins: in0=end_MM, in1=First_Instruction, in2=En_Inst0, out=open
  Demultiplexer #(.enable("false")) demultiplexer_16 (
    .out0(demultiplexer_16_out0), .out1(demultiplexer_16_out1), .in(demultiplexer_17_out0), .sel(Wr));
  Demultiplexer #(.enable("false")) demultiplexer_17 (
    .out0(demultiplexer_17_out0), .out1(demultiplexer_17_out1), .in(wait_rf), .sel(or_25_out));
  or or_25 (or_25_out, lw, pop);
  Demultiplexer #(.enable("false")) demultiplexer_18 (
    .out0(demultiplexer_18_out0), .out1(demultiplexer_18_out1), .in(demultiplexer_17_out1), .sel(pop));
  or or_26 (or_26_out, demultiplexer_23_out0, demultiplexer_11_out1);
  or or_27 (or_27_out, demultiplexer_24_out0, demultiplexer_12_out1);
  or or_28 (or_28_out, demultiplexer_25_out0, demultiplexer_49_out1);
  or or_29 (or_29_out, SDI0_1, demultiplexer_19_out0);
  Demultiplexer #(.enable("false")) demultiplexer_19 (
    .out0(demultiplexer_19_out0), .out1(demultiplexer_19_out1), .in(demultiplexer_14_out1), .sel(not_7_out));
  not not_7 (not_7_out, lw);
  Demultiplexer #(.enable("false")) demultiplexer_20 (
    .out0(SSP0_0), .out1(demultiplexer_20_out1), .in(demultiplexer_19_out1), .sel(not_8_out));
  not not_8 (not_8_out, push);
  Demultiplexer #(.enable("false")) demultiplexer_21 (
    .out0(BCS1_0), .out1(demultiplexer_21_out1), .in(demultiplexer_15_out1), .sel(not_9_out));
  not not_9 (not_9_out, bne);
  Demultiplexer #(.enable("false")) demultiplexer_22 (
    .out0(demultiplexer_22_out0), .out1(demultiplexer_22_out1), .in(demultiplexer_16_out1), .sel(push));
  or or_30 (or_30_out, SRT2, demultiplexer_18_out0);
  D_Flip_Flop Wait_MM_3 (.clk(Clock), .D(or_26_out), .Q(Wait_MM_3_q), .reset(rst));  // open: Qn, preset, en
  Demultiplexer #(.enable("false")) demultiplexer_23 (
    .out0(demultiplexer_23_out0), .out1(demultiplexer_23_out1), .in(Wait_MM_3_q), .sel(or_37_out));
  Demultiplexer #(.enable("false")) demultiplexer_24 (
    .out0(demultiplexer_24_out0), .out1(demultiplexer_24_out1), .in(Wait_MM_4_q), .sel(or_31_out));
  D_Flip_Flop Wait_MM_4 (.clk(Clock), .D(or_27_out), .Q(Wait_MM_4_q), .reset(rst));  // open: Qn, preset, en
  or or_31 (or_31_out, end_MM, ~First_Instruction, En_Inst0);  // OR_Gate
  Demultiplexer #(.enable("false")) demultiplexer_25 (
    .out0(demultiplexer_25_out0), .out1(demultiplexer_25_out1), .in(Idle_9_q), .sel(start));
  D_Flip_Flop Idle_9 (.clk(Clock), .D(or_28_out), .Q(Idle_9_q), .preset(rst));  // open: Qn, en, reset
  D_Flip_Flop u_End_RT (.clk(Clock), .D(or_32_out), .Q(End_RT_q), .reset(rst));  // open: Qn, preset, en
  or or_32 (or_32_out, SDI0_0, demultiplexer_13_out0);
  D_Flip_Flop End_RT_2 (.clk(Clock), .D(or_29_out), .Q(End_RT_2_q), .reset(rst));  // open: Qn, preset, en
  Demultiplexer #(.enable("false")) demultiplexer_26 (.out0(SDI0_1), .out1(o2), .in(End_RT_2_q), .sel(End_RT));
  Demultiplexer #(.enable("false")) demultiplexer_27 (
    .out0(demultiplexer_27_out0), .out1(demultiplexer_27_out1), .in(demultiplexer_20_out1), .sel(not_10_out));
  not not_10 (not_10_out, sw);
  Demultiplexer #(.enable("false")) demultiplexer_28 (
    .out0(BCS0_1), .out1(demultiplexer_28_out1), .in(demultiplexer_21_out1), .sel(not_11_out));
  not not_11 (not_11_out, blez);
  Demultiplexer #(.enable("false")) demultiplexer_29 (
    .out0(BCS2_0), .out1(demultiplexer_29_out1), .in(demultiplexer_28_out1), .sel(not_12_out));
  not not_12 (not_12_out, bgtz);
  or or_33 (or_33_out, wait_branch, demultiplexer_16_out0, End_WT, End_RT);
  or or_34 (or_34_out, ALUSB1, demultiplexer_22_out0);
  or or_35 (or_35_out, minus_RW1, demultiplexer_22_out1);
  D_Flip_Flop Read_Time (.clk(Clock), .D(or_30_out), .Q(MMS0_2), .reset(rst));  // open: Qn, preset, en
  D_Flip_Flop Pop_Read_Time (.clk(Clock), .D(or_36_out), .Q(MMS1_1), .reset(rst));  // open: Qn, preset, en
  or or_36 (or_36_out, SRT3, demultiplexer_18_out1);
  Demultiplexer #(.enable("false")) demultiplexer_30 (
    .out0(demultiplexer_30_out0), .out1(KBD_Enable), .in(demultiplexer_23_out1), .sel(kbd));
  or or_37 (or_37_out, end_MM, ~First_Instruction, En_Inst0);  // OR_Gate
  Demultiplexer #(.enable("false")) demultiplexer_31 (
    .out0(demultiplexer_31_out0), .out1(TTY_Enable), .in(demultiplexer_24_out1), .sel(tty));
  or or_38 (or_38_out, demultiplexer_41_out0, demultiplexer_25_out1);
  Demultiplexer #(.enable("false")) demultiplexer_32 (.out0(SDI0_0), .out1(o0), .in(End_RT_q), .sel(End_RT));
  D_Flip_Flop u_End_WT (.clk(Clock), .D(or_39_out), .Q(End_WT_q), .reset(rst));  // open: Qn, preset, en
  or or_39 (or_39_out, demultiplexer_42_out0, SSP0_0);
  D_Flip_Flop End_WT_2 (.clk(Clock), .D(or_40_out), .Q(End_WT_2_q), .reset(rst));  // open: Qn, preset, en
  or or_40 (or_40_out, demultiplexer_43_out0, demultiplexer_27_out0);
  Demultiplexer #(.enable("false")) demultiplexer_33 (
    .out0(o5), .out1(demultiplexer_33_out1), .in(demultiplexer_27_out1), .sel(not_13_out));
  not not_13 (not_13_out, mfhi);
  Demultiplexer #(.enable("false")) demultiplexer_34 (
    .out0(o6), .out1(F), .in(demultiplexer_33_out1), .sel(not_14_out));
  not not_14 (not_14_out, mflo);
  Demultiplexer #(.enable("false")) demultiplexer_35 (
    .out0(BCS0_2), .out1(En_PC5), .in(demultiplexer_29_out1), .sel(not_15_out));
  not not_15 (not_15_out, bltz);
  Demultiplexer #(.enable("false")) demultiplexer_36 (.out0(wait_branch), .out1(MMS0_0), .in(PC_q), .sel(End_BCU));
  D_Flip_Flop PC (.clk(Clock), .D(or_33_out), .Q(PC_q), .reset(rst));  // open: Qn, preset, en
  Demultiplexer #(.enable("false")) demultiplexer_37 (
    .out0(ALUSB1), .out1(demultiplexer_37_out1), .in(Write_Time_q), .sel(WT__0));
  D_Flip_Flop Write_Time (.clk(Clock), .D(or_34_out), .Q(Write_Time_q), .reset(rst));  // open: Qn, preset, en
  Demultiplexer #(.enable("false")) demultiplexer_38 (
    .out0(minus_RW1), .out1(demultiplexer_38_out1), .in(Push_Write_Time_q), .sel(WT__0));
  D_Flip_Flop Push_Write_Time (.clk(Clock), .D(or_35_out), .Q(Push_Write_Time_q), .reset(rst));  // open: Qn, preset, en
  Demultiplexer #(.enable("false")) demultiplexer_39 (.out0(SRT2), .out1(RW1), .in(MMS0_2), .sel(RT__0));
  Demultiplexer #(.enable("false")) demultiplexer_40 (.out0(SRT3), .out1(RW0), .in(MMS1_1), .sel(RT__0));
  Demultiplexer #(.enable("false")) demultiplexer_41 (
    .out0(demultiplexer_41_out0), .out1(demultiplexer_41_out1), .in(Wait_MM_5_q), .sel(wait_rf));
  D_Flip_Flop Wait_MM_5 (.clk(Clock), .D(or_38_out), .Q(Wait_MM_5_q), .reset(rst));  // open: Qn, preset, en
  Demultiplexer #(.enable("false")) demultiplexer_42 (
    .out0(demultiplexer_42_out0), .out1(o3), .in(End_WT_q), .sel(End_WT));
  Demultiplexer #(.enable("false")) demultiplexer_43 (
    .out0(demultiplexer_43_out0), .out1(o4), .in(End_WT_2_q), .sel(End_WT));
  or or_41 (or_41_out, demultiplexer_45_out0, demultiplexer_30_out0, KBD_Enable);
  or or_42 (or_42_out, demultiplexer_46_out0, demultiplexer_31_out0, TTY_Enable);
  Demultiplexer #(.enable("false")) demultiplexer_44 (
    .out0(ALUSB0), .out1(demultiplexer_44_out1), .in(demultiplexer_41_out1), .sel(or_23_out));
  or or_43 (or_43_out, demultiplexer_47_out0, BCS0_0, BCS1_0, BCS0_1, BCS2_0, BCS0_2, En_PC5);
  or or_44 (or_44_out, SRT1, MMS0_0);
  or or_45 (or_45_out, End_WT, demultiplexer_37_out1, demultiplexer_38_out1);
  or or_46 (or_46_out, End_RT, RW1, RW0);
  Demultiplexer #(.enable("false")) demultiplexer_45 (
    .out0(demultiplexer_45_out0), .out1(demultiplexer_45_out1), .in(End_q), .sel(start));
  D_Flip_Flop End (.clk(Clock), .D(or_41_out), .Q(End_q), .reset(rst));  // open: Qn, preset, en
  Demultiplexer #(.enable("false")) demultiplexer_46 (
    .out0(demultiplexer_46_out0), .out1(demultiplexer_46_out1), .in(End_2_q), .sel(start));
  D_Flip_Flop End_2 (.clk(Clock), .D(or_42_out), .Q(End_2_q), .reset(rst));  // open: Qn, preset, en
  Demultiplexer #(.enable("false")) demultiplexer_47 (
    .out0(demultiplexer_47_out0), .out1(demultiplexer_47_out1), .in(End_Instruction_q), .sel(End_RF));
  D_Flip_Flop End_Instruction (.clk(Clock), .D(or_43_out), .Q(End_Instruction_q), .reset(rst));  // open: Qn, preset, en
  D_Flip_Flop Read_Time_2 (.clk(Clock), .D(or_44_out), .Q(Read_Time_2_q), .reset(rst));  // open: Qn, preset, en
  Demultiplexer #(.enable("false")) demultiplexer_48 (
    .out0(SRT1), .out1(demultiplexer_48_out1), .in(Read_Time_2_q), .sel(RT__0));
  D_Flip_Flop End_3 (.clk(Clock), .D(or_45_out), .Q(End_WT), .reset(or_47_out));  // open: Qn, preset, en
  or or_47 (or_47_out, MMS0_0, rst);
  D_Flip_Flop End_4 (.clk(Clock), .D(or_46_out), .Q(End_RT), .reset(or_48_out));  // open: Qn, preset, en
  or or_48 (or_48_out, MMS0_0, rst);
  D_Flip_Flop End_5 (.clk(Clock), .D(or_49_out), .Q(End_5_q), .reset(rst));  // open: Qn, preset, en
  or or_49 (or_49_out, end_ALU, ALUSB0, demultiplexer_44_out1);
  or or_50 (ALUSB, ALUSB0, ALUSB1);
  or or_51 (or_51_out, o0, o2, o5, o6, o7, o8, o9, o10);
  or or_52 (Selector_Data_Input[0], SDI0_0, SDI0_1, o5, o9);
  or or_53 (Selector_Data_Input[1], SDI0_0, SDI0_1, o8, o7);
  or or_54 (Selector_Data_Input[2], o8, o9, o10);
  or or_55 (or_55_out, End_BCU, demultiplexer_47_out1);
  or or_56 (or_56_out, end_MM, demultiplexer_48_out1);
  Demultiplexer #(.enable("false")) demultiplexer_49 (
    .out0(end_ALU), .out1(demultiplexer_49_out1), .in(End_5_q), .sel(start));
  D_Flip_Flop Update_Values (.clk(Clock), .D(or_51_out), .Q(Update_Values_q), .reset(rst));  // open: Qn, preset, en
  D_Flip_Flop End_6 (.clk(Clock), .D(or_55_out), .Q(End_6_q), .reset(rst));  // open: Qn, preset, en
  or or_57 (Enabled_PC, BCS0_0, BCS1_0, BCS0_1, BCS2_0, BCS0_2, En_PC5);
  Demultiplexer #(.enable("false")) demultiplexer_50 (
    .out0(end_MM), .out1(demultiplexer_50_out1), .in(End_7_q), .sel(start));
  D_Flip_Flop End_7 (.clk(Clock), .D(or_56_out), .Q(End_7_q), .reset(rst));  // open: Qn, preset, en
  or or_58 (or_58_out, End_RF, Update_Values_q, o1, o3, o4);
  or or_59 (Stack_Point_Selector[0], SSP0_0, rst);
  or or_60 (Stack_Point_Selector[1], o0, SSP0_0);
  or or_61 (CURW, RW0, RW1, o5, o6, o7, o8, o9, o10);
  Demultiplexer #(.enable("false")) demultiplexer_51 (
    .out0(End_BCU), .out1(demultiplexer_51_out1), .in(End_6_q), .sel(start));
  D_Flip_Flop End_8 (.clk(Clock), .D(or_58_out), .Q(End_8_q), .reset(rst));  // open: Qn, preset, en
  Demultiplexer #(.enable("false")) demultiplexer_52 (
    .out0(End_RF), .out1(demultiplexer_52_out1), .in(End_8_q), .sel(start));

  // Other names for the same wires on the sheet: BCS[2:0] = Branch_Control_Selector; clk = Clock;
  //   En_Inst = Enable_Inst; En_PC = Enabled_PC; En_PC0 = BCS0_0; En_PC1 = BCS1_0; BCS1_1 = BCS0_1; En_PC2 = BCS0_1;
  //   En_PC3 = BCS2_0; BCS2_1 = BCS0_2; En_PC4 = BCS0_2; End_FI = En_Inst0; FI = First_Instruction;
  //   KBD_Available = KBD_Avalaible; SSP1_0 = o0; RW2 = o5; SDI0_2 = o5; RW3 = o6; RW4 = o7; SDI1_2 = o7; RW5 = o8;
  //   SDI1_3 = o8; SDI2_0 = o8; RW6 = o9; SDI0_3 = o9; SDI2_1 = o9; RW7 = o10; SDI2_2 = o10; SSP0_1 = rst;
  //   rst_RT = MMS0_0; rst_WT = MMS0_0; RW = CURW; SDI[2:0] = Selector_Data_Input; SDI1_0 = SDI0_0; SDI1_1 = SDI0_1;
  //   SSP[1:0] = Stack_Point_Selector; SSP1_1 = SSP0_0; minus_RW0 = ALUSB1; MMS0_1 = ALUSB1; SWT0 = ALUSB1;
  //   MMS1_0 = minus_RW1; SWT1 = minus_RW1

  // Notes on the sheet:
  //   Control Unit Register File
  //   Control Unit TTY
  //   Control Unit Memory Manager
  //   Control Unit Keyboard
  //   Control Unit Branch Control
  //   Control Unit ALU
endmodule
