// Logisim project cu.circ as structural Verilog: 1 circuit, main circuit bc
module bc (
  input  [31:0] Current_Address_Instruction,
  input  [31:0] K,
  input  [31:0] Current_Inst,
  input  [31:0] Jump_Register,
  input  jmp,
  input  FC,
  input  JMP_Inst,
  input  JR_Inst,
  output [31:0] out_9
);

  wire and_1_out, priority_encoder_1_en_out;
  wire [1:0] multiplexer_1_out, priority_encoder_1_out;
  wire [31:0] adder_1_out, adder_2_out;

  and and_1 (and_1_out, jmp, FC);
  Adder #(.width(32)) adder_1 (.a(32'h4), .b(Current_Address_Instruction), .out(adder_1_out));  // open: cin, cout
  Adder #(.width(32)) adder_2 (.a(Current_Address_Instruction), .b(K), .out(adder_2_out));  // open: cin, cout
  Priority_Encoder #(.select(2)) priority_encoder_1 (
    .in1(and_1_out), .in2(JMP_Inst), .in3(JR_Inst), .out(priority_encoder_1_out),
    .en_out(priority_encoder_1_en_out));  // open: in0, gs, en_in
  Multiplexer #(.width(2), .enable("false")) multiplexer_1 (
    .in0(priority_encoder_1_out), .in1(2'b00), .out(multiplexer_1_out), .sel(priority_encoder_1_en_out));
  Multiplexer #(.select(2), .width(32), .enable("false")) multiplexer_2 (
    .in0(adder_1_out), .in1(adder_2_out),
    .in2({Current_Address_Instruction[31:28], Current_Inst[25:0], 2'b00}), .in3(Jump_Register), .out(out_9),
    .sel(multiplexer_1_out));

  // Notes on the sheet:
  //   INPUTS:
  //   OUTPUT:
endmodule
